# Fritzing sketch SirenFritz (saved by Fritzing 0.9.2b)
breadboards: 1

parts:
  BeagleBone1 = BeagleBone Black
  Q1 = NPN-Transistor [package="TO92 [THT]"]
  R1 = Resistor [tolerance=±5% resistance=10 package="2512 [SMD]"]
  SP1 = SPEAKER [package=pcb_mount_speaker]

nets:
  N1: BeagleBone1.no_name_yet#1, Q1.E
  N2: BeagleBone1.no_name_yet#5, SP1.-
  N3: BeagleBone1.no_name_yet#10, R1.Pin_1
  N4: Q1.B, R1.Pin_0
  N5: Q1.C, SP1.+

custom parts:
  BeagleBone Black: BeagleBone Black rev. A5B
