# Fritzing sketch flashESP8266-01 (saved by Fritzing 0.9.2b)
breadboards: 1

parts:
  Part1 = FTDI Basic Programmer
  U1 = ESP8266 WiFi Module [part_number=ESP8266]
  R1 = Resistor [tolerance=±5% resistance=10k package=THT]
  R2 = Resistor [tolerance=±5% resistance=10k package=THT]
  FLSH = Momentary Switch [package=ksa_sealed_tac_switch]
  RST = Momentary Switch [package=ksa_sealed_tac_switch]
  VCC1 = Battery
  C1 = Capacitor Polarized [package=panasonic_c]
  C2 = Ceramic Capacitor [capacitance="100 nF" package="0603 [SMD, multilayer]"]
  CHPD = Momentary Switch [package=ksa_sealed_tac_switch]

nets:
  N1: Part1.GND, FLSH.1, RST.2, VCC1.-, C1.-, C2.1, CHPD.2
  N2: U1.GPIO_0, FLSH.3
  N3: R1.Pin_0, CHPD.4
  N4: R1.Pin_1, R2.Pin_0, VCC1.+, C1.+, C2.0
  N5: R2.Pin_1, RST.4

notes:
  Press the FLSH button before you initiate a flash, release it as you see the flashing safely started. RST is not necessary with the FDTI because it is effectively pressed by the DTR, but it you are using an FDTI without DTR control you need to press RST first, then FLSH.
  The CHPD button is used to tell the remote switch program to send an event, this is effectively the 'switch'. If fires when you release it rather than when you press it.

custom parts:
  ESP8266 WiFi Module: Generic WiFi Module based on the ESP8266 with onboard PCB antenna and UART communications
